// Logisim project NAND AND NOR ALL GATE.circ as structural Verilog: 1 circuit, main circuit main
module main (
  input  in_1,
  input  in_2,
  input  _2___NOT_GATE,
  input  in_4,
  input  _2_NAND_TO_NOT,
  input  in_6,
  input  _3_NAND_TO_OR,
  input  in_8,
  input  in_9,
  input  in_10,
  input  in_11,
  input  _4_nand_using_nor,
  input  in_13,
  input  in_14,
  input  _5_and_using_nor,
  input  _5_Nor_using_nand,
  input  in_17,
  input  in_18,
  input  _6_xor_using_nand,
  input  in_20,
  input  in_21,
  input  in_22,
  output out_23,
  output out_24,
  output out_25,
  output out_26,
  output out_27,
  output out_28,
  output out_29,
  output out_30,
  output out_31,
  output out_32,
  output out_33,
  output out_34,
  output out_35,
  output out_36
);

  wire nand_3_out, nand_4_out, nand_5_out, nand_6_out, nand_7_out, nand_9_out, nand_10_out, nand_11_out,
       nand_12_out, nand_13_out, nand_14_out, nand_15_out, nor_1_out, nor_2_out, nor_3_out, nor_4_out,
       nor_5_out, nor_6_out, nor_7_out, nor_8_out, nor_9_out, nor_10_out, nor_12_out, nor_15_out, nor_16_out,
       nor_17_out;

  nand nand_1 (out_27, _3_NAND_TO_OR, _3_NAND_TO_OR);
  nand nand_2 (out_30, in_9, in_9);
  nand nand_3 (nand_3_out, _5_Nor_using_nand, _5_Nor_using_nand);
  nand nand_4 (nand_4_out, in_18, in_18);
  nand nand_5 (nand_5_out, _6_xor_using_nand, _6_xor_using_nand);
  nand nand_6 (nand_6_out, in_21, in_21);
  nand nand_7 (nand_7_out, in_2, in_4);
  nand nand_8 (out_25, _2_NAND_TO_NOT, _2_NAND_TO_NOT);
  nand nand_9 (nand_9_out, in_11, in_13);
  nand nand_10 (nand_10_out, in_11, in_11);
  nand nand_11 (nand_11_out, in_13, in_13);
  nand nand_12 (nand_12_out, nand_10_out, nand_11_out);
  nand nand_13 (nand_13_out, nand_3_out, nand_4_out);
  nand nand_14 (nand_14_out, nand_5_out, in_21);
  nand nand_15 (nand_15_out, nand_6_out, _6_xor_using_nand);
  nand nand_16 (out_24, nand_7_out, nand_7_out);
  nand nand_17 (out_28, out_27, out_30);
  nand nand_18 (out_34, nand_13_out, nand_13_out);
  nand nand_19 (out_35, nand_14_out, nand_15_out);
  nand nand_20 (out_31, nand_9_out, nand_12_out);
  nor nor_1 (nor_1_out, in_1, _2___NOT_GATE);
  nor nor_2 (nor_2_out, in_8, in_8);
  nor nor_3 (nor_3_out, in_10, in_10);
  nor nor_4 (nor_4_out, _4_nand_using_nor, _4_nand_using_nor);
  nor nor_5 (nor_5_out, in_14, in_14);
  nor nor_6 (nor_6_out, _5_and_using_nor, in_17);
  nor nor_7 (nor_7_out, _5_and_using_nor, _5_and_using_nor);
  nor nor_8 (nor_8_out, in_17, in_17);
  nor nor_9 (nor_9_out, in_20, in_20);
  nor nor_10 (nor_10_out, in_22, in_22);
  nor nor_11 (out_26, in_6, in_6);
  nor nor_12 (nor_12_out, nor_9_out, nor_10_out);
  nor nor_13 (out_23, nor_1_out, nor_1_out);
  nor nor_14 (out_29, nor_2_out, nor_3_out);
  nor nor_15 (nor_15_out, nor_4_out, in_14);
  nor nor_16 (nor_16_out, nor_5_out, _4_nand_using_nor);
  nor nor_17 (nor_17_out, nor_7_out, nor_8_out);
  nor nor_18 (out_32, nor_15_out, nor_16_out);
  nor nor_19 (out_33, nor_6_out, nor_17_out);
  nor nor_20 (out_36, nor_12_out, nor_12_out);

  // Notes on the sheet:
  //   4.nand using nand
  //   5.
  //   NAND GATEB TO ALL OTHER GATE
  //   1.NAND TO AND GATE 
  //   6.nand using nor
  //   NOR GATE
  //   1 . NOR TO OR GATE
  //   3. AND GATE
endmodule
