// Logisim project halfadder.circ as structural Verilog: 1 circuit, main circuit main
module main (
  input  in_1,
  input  in_2,
  output out_3,
  output out_4
);

  wire undriven, undriven_2;

  xor xor_1 (out_3, undriven, undriven_2);
  and and_1 (out_4, undriven, undriven_2);
endmodule
