// Logisim project lab2.circ as structural Verilog: 1 circuit, main circuit main
module main (
  input  in_1,
  input  in_2,
  input  in_3,
  input  in_4,
  input  in_5,
  input  in_6,
  input  in_7,
  input  in_8,
  input  in_9,
  input  in_10,
  input  in_11,
  input  in_12,
  input  in_13,
  input  in_14,
  input  in_15,
  input  in_16,
  input  in_17,
  input  in_18,
  output out_19,
  output out_20,
  output out_21,
  output out_22,
  output out_23,
  output out_24,
  output out_25,
  output out_26,
  output out_27,
  output out_28,
  output out_29,
  output out_30
);

  wire nand_1_out, nand_2_out, nand_3_out, nand_7_out, nand_8_out, nand_9_out, nand_10_out, nand_14_out,
       nor_1_out, nor_2_out, nor_3_out, nor_5_out, nor_6_out, nor_7_out, nor_8_out, nor_9_out, nor_10_out,
       nor_13_out;

  nand nand_1 (nand_1_out, in_11, in_12);
  nand nand_2 (nand_2_out, in_15, in_16);
  nand nand_3 (nand_3_out, in_1, in_3);
  nand nand_4 (out_21, in_5, in_5);
  nand nand_5 (out_23, in_7, in_7);
  nand nand_6 (out_26, in_9, in_9);
  nand nand_7 (nand_7_out, in_11, nand_1_out);
  nand nand_8 (nand_8_out, nand_1_out, in_12);
  nand nand_9 (nand_9_out, in_15, nand_2_out);
  not nand_10 (nand_10_out, nand_2_out);  // NAND_Gate
  nand nand_11 (out_19, nand_3_out, nand_3_out);
  nand nand_12 (out_27, nand_7_out, nand_8_out);
  nand nand_13 (out_24, out_23, out_26);
  nand nand_14 (nand_14_out, nand_9_out, nand_10_out);
  nand nand_15 (out_29, nand_14_out, nand_14_out);
  nor nor_1 (nor_1_out, in_13, in_14);
  nor nor_2 (nor_2_out, in_17, in_18);
  nor nor_3 (nor_3_out, in_2, in_4);
  nor nor_4 (out_22, in_6, in_6);
  nor nor_5 (nor_5_out, in_8, in_8);
  nor nor_6 (nor_6_out, in_10, in_10);
  nor nor_7 (nor_7_out, in_13, nor_1_out);
  nor nor_8 (nor_8_out, nor_1_out, in_14);
  nor nor_9 (nor_9_out, in_17, nor_2_out);
  nor nor_10 (nor_10_out, nor_2_out, in_18);
  nor nor_11 (out_20, nor_3_out, nor_3_out);
  nor nor_12 (out_25, nor_5_out, nor_6_out);
  nor nor_13 (nor_13_out, nor_7_out, nor_8_out);
  nor nor_14 (out_30, nor_9_out, nor_10_out);
  nor nor_15 (out_28, nor_13_out, nor_13_out);

  // Notes on the sheet:
  //   1.NAND TO AND GATE 
  //   2.NAND TO NOT
  //   3.NAND TO OR
  //   NAND GATEB TO ALL OTHER GATE
  //   xor gate
  //   xnor gate
  //   2 . NOT GATE 
  //   3. AND GATE
  //   xor gate
  //   NOR GATE
  //   1 . NOR TO OR GATE
  //   xnor gate
endmodule
