// Logisim project MULTIPLIXER AND DEMULTIPLIXER.circ as structural Verilog: 1 circuit, main circuit main
module main (
  input  X,
  input  x_2,
  input  a,
  input  Y,
  input  y_2,
  input  Z,
  input  A_2,
  input  b,
  input  B_2,
  input  c,
  input  C_2,
  input  d,
  input  D_2,
  input  E,
  input  x_3,
  input  a_3,
  input  y_3,
  input  F,
  input  G,
  input  H,
  input  X_4,
  input  Y_4,
  input  Z_2,
  input  A_4,
  output out_25,
  output out_26,
  output out_27,
  output out_28,
  output out_29,
  output out_30,
  output out_31,
  output out_32,
  output out_33,
  output out_34,
  output out_35,
  output out_36,
  output out_37,
  output out_38
);

  wire and_1_out, and_2_out, and_3_out, and_4_out, and_9_out, and_10_out, and_11_out, and_12_out, and_13_out,
       and_14_out, and_15_out, and_16_out, not_1_out, not_2_out, not_3_out, not_4_out, not_5_out, not_6_out,
       not_7_out, not_8_out, not_9_out, not_10_out;

  not not_1 (not_1_out, x_2);
  not not_2 (not_2_out, y_2);
  not not_3 (not_3_out, x_3);
  not not_4 (not_4_out, y_3);
  and and_1 (and_1_out, not_1_out, a, not_2_out);
  and and_2 (and_2_out, not_1_out, b, y_2);
  and and_3 (and_3_out, x_2, c, not_2_out);
  and and_4 (and_4_out, x_2, d, y_2);
  and and_5 (out_27, not_3_out, a_3, not_4_out);
  and and_6 (out_28, not_3_out, a_3, y_3);
  and and_7 (out_29, x_3, a_3, not_4_out);
  and and_8 (out_30, x_3, a_3, y_3);
  or or_1 (out_25, and_1_out, and_2_out, and_3_out, and_4_out);
  not not_5 (not_5_out, X);
  not not_6 (not_6_out, Y);
  not not_7 (not_7_out, Z);
  not not_8 (not_8_out, X_4);
  not not_9 (not_9_out, Y_4);
  not not_10 (not_10_out, Z_2);
  and and_9 (and_9_out, not_5_out, not_6_out, not_7_out, A_2);
  and and_10 (and_10_out, not_5_out, not_6_out, Z, B_2);
  and and_11 (and_11_out, not_5_out, not_6_out, Z, C_2);
  and and_12 (and_12_out, not_6_out, Y, not_7_out, D_2);
  and and_13 (and_13_out, not_6_out, Y, Z, E);
  and and_14 (and_14_out, X, not_6_out, Z, F);
  and and_15 (and_15_out, X, Y, not_7_out, G);
  and and_16 (and_16_out, X, Y, Z, H);
  and and_17 (out_31, not_8_out, not_9_out, not_10_out, A_4);
  and and_18 (out_32, not_8_out, not_9_out, Z_2, A_4);
  and and_19 (out_33, not_8_out, not_9_out, Z_2, A_4);
  and and_20 (out_34, not_9_out, Y_4, not_10_out, A_4);
  and and_21 (out_35, not_9_out, Y_4, Z_2, A_4);
  and and_22 (out_36, X_4, not_9_out, Z_2, A_4);
  and and_23 (out_37, X_4, Y_4, not_10_out, A_4);
  and and_24 (out_38, X_4, Y_4, Z_2, A_4);
  or or_2 (out_26, and_9_out, and_10_out, and_11_out, and_12_out, and_13_out, and_14_out, and_15_out, and_16_out);

  // Notes on the sheet:
  //   Multiplixer 4*1
  //   Demultiplixer 1*4
  //   Multiplixer 8*1
  //   Deultiplixer 8*1
endmodule
