// Logisim project 4BITALU.circ as structural Verilog: 1 circuit, main circuit main
module main (
  input  X,
  input  Y,
  input  A,
  input  B,
  input  C,
  input  D,
  input  X_2,
  input  Y_2,
  input  E,
  input  A_2,
  input  F,
  input  B_2,
  input  C_2,
  input  G,
  input  D_2,
  input  H,
  input  E_2,
  input  F_2,
  input  G_2,
  input  H_2,
  output OUTPUT,
  output out_22,
  output CARRY,
  output CARRY_2
);

  wire and_1_out, and_3_out, and_4_out, and_5_out, and_6_out, and_7_out, and_9_out, and_10_out, and_11_out,
       and_12_out, not_1_out, not_2_out, not_3_out, not_4_out, not_5_out, or_1_out, or_3_out, xor_1_out,
       xor_2_out, xor_3_out, xor_4_out;

  and and_1 (and_1_out, A, B);
  or or_1 (or_1_out, C, D);
  xor xor_1 (xor_1_out, E, F);
  not not_1 (not_1_out, X);
  xor xor_2 (xor_2_out, G, H);
  and and_2 (CARRY, G, H);
  not not_2 (not_2_out, Y);
  and and_3 (and_3_out, not_1_out, not_2_out, and_1_out);
  and and_4 (and_4_out, not_2_out, X, or_1_out);
  and and_5 (and_5_out, Y, not_1_out, xor_1_out);
  and and_6 (and_6_out, Y, X, xor_2_out);
  or or_2 (OUTPUT, and_3_out, and_4_out, and_5_out, and_6_out);
  not not_3 (not_3_out, G_2);
  and and_7 (and_7_out, A_2, B_2);
  or or_3 (or_3_out, C_2, D_2);
  xor xor_3 (xor_3_out, E_2, F_2);
  xor xor_4 (xor_4_out, G_2, H_2);
  and and_8 (CARRY_2, not_3_out, H_2);
  not not_4 (not_4_out, X_2);
  not not_5 (not_5_out, Y_2);
  and and_9 (and_9_out, not_4_out, not_5_out, and_7_out);
  and and_10 (and_10_out, not_5_out, X_2, or_3_out);
  and and_11 (and_11_out, Y_2, not_4_out, xor_3_out);
  and and_12 (and_12_out, Y_2, X_2, xor_4_out);
  or or_4 (out_22, and_9_out, and_10_out, and_11_out, and_12_out);

  // Notes on the sheet:
  //   4 BIT ALU
  //   4 BIT ALU
  //   OUTPUT
endmodule
