// Logisim project dpa-logisim.circ as structural Verilog: 1 circuit, main circuit main
module main (
  input  [3:0] Address,
  input  Sel,
  input  in_3,
  input  in_4,
  input  in_5,
  input  in_6,
  input  in_7,
  input  in_8,
  input  [3:0] in_9,
  input  [3:0] Sel_2,
  input  [3:0] Sel_3,
  input  in_12,
  output [3:0] Instruction_Reg,
  output [3:0] out_14,
  output [3:0] Data_Reg1,
  output [3:0] out_16,
  output [3:0] out_17,
  output [3:0] OUTPUT,
  output [3:0] out_19
);

  wire clock_1_out, clock_2_out;
  wire [3:0] adder_1_out, multiplexer_1_out, multiplexer_2_out, subtractor_1_out;

  Demultiplexer #(.width(4)) demultiplexer_1 (
    .out0(Instruction_Reg), .out1(out_14), .in(OUTPUT), .sel(in_3));  // open: en
  Register #(.width(4)) register_1 (.D(OUTPUT), .en(in_5), .Q(Data_Reg1), .clk(clock_1_out));  // open: clr
  Register #(.width(4)) register_2 (.D(OUTPUT), .en(in_7), .Q(out_17), .clk(clock_1_out));  // open: clr
  Counter #(.width(4), .max('hf)) counter_1 (
    .load(in_8), .D(in_9), .count(in_12), .Q(out_19), .clk(clock_1_out));  // open: carry, clr
  Clock clock_1 (.out(clock_1_out));
  Multiplexer #(.select(4), .width(4)) multiplexer_1 (
    .in0(out_17), .in1(out_19), .out(multiplexer_1_out), .sel(Sel_2));  // open: in2, in3, in4, in5, in6, in7, in8, in9, in10, in11, in12, in13, in14, in15, en
  Adder #(.width(4)) adder_1 (.a(Data_Reg1), .b(multiplexer_1_out), .out(adder_1_out));  // open: cin, cout
  Subtractor #(.width(4)) subtractor_1 (
    .a(Data_Reg1), .b(multiplexer_1_out), .out(subtractor_1_out));  // open: bin, bout
  Multiplexer #(.select(4), .width(4)) multiplexer_2 (
    .in0(adder_1_out), .in1(subtractor_1_out), .in2(multiplexer_1_out), .out(multiplexer_2_out), .sel(Sel_3));  // open: in3, in4, in5, in6, in7, in8, in9, in10, in11, in12, in13, in14, in15, en
  Multiplexer #(.width(4)) multiplexer_3 (.in0(out_16), .in1(multiplexer_2_out), .out(OUTPUT), .sel(in_6));  // open: en
  Clock clock_2 (.out(clock_2_out));
  RAM #(.addrWidth(4), .dataWidth(4)) ram_1 (
    .addr(Address), .data(out_16), .sel(Sel), .clk(clock_2_out), .ld(in_4));  // open: clr

  // Notes on the sheet:
  //          Data Reg2
  //   Program Counter
  //   clk
  //           Address Reg
  //                                                     DATA PATH ARCHITECTURE
  //             ALU
  //   a
  //    b
  //   a
  //   Add
  //         Sub
  //   b
  //               ALU Out
  //       RAM
  //   CLk
  //       Load
endmodule
