// Logisim project halfadder+subtractor+.circ as structural Verilog: 1 circuit, main circuit main
module main (
  input  A,
  input  A_2,
  input  B,
  input  B_2,
  input  A_3,
  input  B_3,
  input  A_4,
  input  B_4,
  input  C,
  input  C_2,
  output sum,
  output differnce,
  output carry,
  output browwo,
  output sum_2,
  output differnce_2,
  output carry_2,
  output browwo_2
);

  wire and_2_out, and_3_out, and_5_out, and_6_out, not_1_out, not_2_out, not_3_out, xor_2_out, xor_5_out;

  xor xor_1 (sum, A, B);
  and and_1 (carry, A, B);
  xor xor_2 (xor_2_out, A_3, B_3);
  and and_2 (and_2_out, A_3, B_3);
  xor xor_3 (sum_2, xor_2_out, C);
  and and_3 (and_3_out, C, xor_2_out);
  or or_1 (carry_2, and_3_out, and_2_out);
  not not_1 (not_1_out, A_2);
  and and_4 (browwo, not_1_out, B_2);
  xor xor_4 (differnce, A_2, B_2);
  not not_2 (not_2_out, A_4);
  xor xor_5 (xor_5_out, A_4, B_4);
  and and_5 (and_5_out, not_2_out, B_4);
  not not_3 (not_3_out, xor_5_out);
  xor xor_6 (differnce_2, xor_5_out, C_2);
  and and_6 (and_6_out, C_2, not_3_out);
  or or_2 (browwo_2, and_6_out, and_5_out);

  // Notes on the sheet:
  //   full adder 
  //   half adder 
  //   sub tractor 
  //   full subtractor
endmodule
