// Logisim project NAND AND NOR ALL GATE.circ as structural Verilog: 1 circuit, main circuit main
module main (
  input  in_1,
  input  in_2,
  input  in_3,
  input  in_4,
  input  in_5,
  input  in_6,
  input  in_7,
  input  in_8,
  input  in_9,
  input  in_10,
  output out_11,
  output out_12,
  output out_13,
  output out_14,
  output out_15,
  output out_16,
  output out_17,
  output out_18
);

  wire nand_1_out, nor_1_out, nor_3_out, nor_4_out;

  nand nand_1 (nand_1_out, in_1, in_3);
  nand nand_2 (out_13, in_5, in_5);
  nand nand_3 (out_15, in_7, in_7);
  nand nand_4 (out_18, in_9, in_9);
  nand nand_5 (out_11, nand_1_out, nand_1_out);
  nand nand_6 (out_16, out_15, out_18);
  nor nor_1 (nor_1_out, in_2, in_4);
  nor nor_2 (out_14, in_6, in_6);
  nor nor_3 (nor_3_out, in_8, in_8);
  nor nor_4 (nor_4_out, in_10, in_10);
  nor nor_5 (out_12, nor_1_out, nor_1_out);
  nor nor_6 (out_17, nor_3_out, nor_4_out);

  // Notes on the sheet:
  //   1.NAND TO AND GATE 
  //   2.NAND TO NOT
  //   3.NAND TO OR
  //   NAND GATEB TO ALL OTHER GATE
  //   2 . NOT GATE 
  //   3. AND GATE
  //   NOR GATE
  //   1 . NOR TO OR GATE
endmodule
